// Logisim project CPU_MIPS.circ as structural Verilog: 3 circuits, main circuit main
module main (
  input  in_1
);

  wire clock, mostrar_1_add, mostrar_1_branch, mostrar_1_jump, mostrar_1_load, mostrar_1_r, mostrar_1_store,
       Reset;
  wire [4:0] separadores_1_rd, separadores_1_rs, separadores_1_rt, separadores_1_shamt;
  wire [5:0] separadores_1_funct, separadores_1_opcode;
  wire [15:0] separadores_1_offset;
  wire [23:0] bit_extender_1_out;
  wire [25:0] separadores_1_jump;
  wire [31:0] adder_1_out, ram_1_data, register_1_q;

  Clock clock_1 (.out(clock));
  Button button_1 (.out(Reset));
  Register #(.width(32)) register_1 (.D(adder_1_out), .en(1'b1), .Q(register_1_q), .clk(clock), .clr(Reset));
  Adder #(.width(32)) adder_1 (.a(32'h1), .b(register_1_q), .out(adder_1_out));  // open: cin, cout
  Bit_Extender #(.in_width(32), .out_width(24)) bit_extender_1 (.in(register_1_q), .out(bit_extender_1_out));
  RAM #(.addrWidth(24), .dataWidth(32)) ram_1 (
    .addr(bit_extender_1_out), .data(ram_1_data));  // open: sel, clk, ld, clr
  // Probe on separadores_1_rd
  // Probe on separadores_1_rt
  // Probe on separadores_1_rs
  // Probe on separadores_1_opcode
  Separadores separadores_1 (
    .in_1(ram_1_data), .Funct(separadores_1_funct), .Shamt(separadores_1_shamt), .RD(separadores_1_rd),
    .RT(separadores_1_rt), .RS(separadores_1_rs), .Opcode(separadores_1_opcode),
    .Offset(separadores_1_offset), .Jump(separadores_1_jump));
  // Probe on separadores_1_jump
  // Probe on separadores_1_offset
  // Probe on separadores_1_shamt
  // Probe on separadores_1_funct
  mostrar mostrar_1 (
    .in_1(separadores_1_opcode), .r(mostrar_1_r), .add(mostrar_1_add), .load(mostrar_1_load),
    .store(mostrar_1_store), .branch(mostrar_1_branch), .Jump(mostrar_1_jump));
  LED led_1 (.in(in_1));
  LED led_2 (.in(mostrar_1_r));
  LED led_3 (.in(mostrar_1_add));
  LED led_4 (.in(mostrar_1_load));
  LED led_5 (.in(mostrar_1_store));
  LED led_6 (.in(mostrar_1_branch));
  LED led_7 (.in(mostrar_1_jump));
endmodule

module Separadores (
  input  [31:0] in_1,
  output [5:0] Funct,
  output [4:0] Shamt,
  output [4:0] RD,
  output [4:0] RT,
  output [4:0] RS,
  output [5:0] Opcode,
  output [15:0] Offset,
  output [25:0] Jump
);


  assign Funct = in_1[5:0];
  assign Jump = in_1[25:0];
  assign Offset = in_1[15:0];
  assign Opcode = in_1[31:26];
  assign RD = in_1[15:11];
  assign RS = in_1[25:21];
  assign RT = in_1[20:16];
  assign Shamt = in_1[10:6];

  // Notes on the sheet:
  //   R
endmodule

module mostrar (
  input  [5:0] in_1,
  output r,
  output add,
  output load,
  output store,
  output branch,
  output Jump
);

  Comparator #(.width(6)) comparator_1 (.a(in_1), .b({6{1'b0}}), .eq(r));  // open: gt, lt
  Comparator #(.width(6)) comparator_2 (.a(in_1), .b({6{1'b0}}), .eq(add));  // open: gt, lt
  Comparator #(.width(6)) comparator_3 (.a(in_1), .b(6'b100011), .eq(load));  // open: gt, lt
  Comparator #(.width(6)) comparator_4 (.a(in_1), .b(6'b101011), .eq(store));  // open: gt, lt
  Comparator #(.width(6)) comparator_5 (.a(in_1), .b(6'b100011), .eq(branch));  // open: gt, lt
  Comparator #(.width(6)) comparator_6 (.a(in_1), .b(6'b000010), .eq(Jump));  // open: gt, lt
endmodule
