// Logisim project CPU_Pipeline.circ as structural Verilog: 17 circuits, main circuit main
module main (
  output [3:0] Selec_de_ALU
);

  wire add, addi, alu_1_zero, and_1_out, brach, clock, des_ex_1_alusrc_out, des_ex_1_branch_out,
       des_ex_1_jump_sel_out, des_ex_1_memread_out, des_ex_1_memtoreg_out, des_ex_1_memwrite_out,
       des_ex_1_regwrite_out, ex_mem_1_alusrc_out, ex_mem_1_branch_out, ex_mem_1_jump_sel_out,
       ex_mem_1_memread_out, ex_mem_1_memtoreg_out, ex_mem_1_memwrite_out, ex_mem_1_regwrite_out,
       ex_mem_1_zero_out, forwarding_unit_1_hazard, hazard_control_1_enable, Jump, load, mem_wr_1_alusrc_out,
       mem_wr_1_memtoreg_out, mem_wr_1_regwrite_out, not_1_out, not_2_out, Reset, store, type_inst_1_r,
       UC_branch, UC_memread, UC_memtoreg, UC_memwrite, UC_regdst, UC_regwrite, undriven;
  wire [1:0] forwarding_unit_1_forwarda, forwarding_unit_1_forwardb, UC_aluop;
  wire [3:0] des_ex_1_selec_de_alu_out;
  wire [4:0] decodificador_1_rd, decodificador_1_rs, decodificador_1_rt, des_ex_1_rd_out, des_ex_1_rs_out,
       des_ex_1_rt_out, ex_mem_1_rd_out, ex_mem_1_rs_out, ex_mem_1_rt_out, ex_mem_1_rw_out, mem_wr_1_rd_out,
       mem_wr_1_rw_out, multiplexer_5_out;
  wire [5:0] decodificador_1_opcode, des_ex_1_out_43, ex_mem_1_opcode_2, Funct, mem_wr_1_out_25;
  wire [15:0] decodificador_1_offset;
  wire [23:0] bit_extender_1_out, bit_extender_3_out, bit_extender_5_out, des_ex_1_pc_1_out, des_ex_1_pc_out,
       ex_mem_1_pc_branch_out, ex_mem_1_pc_out, if_dec_1_pc_1_out, if_dec_1_pc_out, mem_wr_1_pc_out,
       multiplexer_1_out, multiplexer_2_out, pc_1, pc_brach_1_pc_brach;
  wire [25:0] decodificador_1_jump, des_ex_1_jump_out, ex_mem_1_jump_out;
  wire [31:0] alu_1_result, bit_extender_2_out, bit_extender_4_out, des_ex_1_offset_out, des_ex_1_r1_out,
       des_ex_1_r2_out, ex_mem_1_r2_out, ex_mem_1_ra_out, if_dec_1_instruccion_in_2, ledinst_1_out_3,
       ledinst_1_out_4, ledinst_1_out_5, ledinst_1_out_6, ledinst_1_out_7, ledinst_2_out_3, ledinst_2_out_4,
       ledinst_2_out_5, ledinst_2_out_6, ledinst_2_out_7, ledinst_3_out_3, ledinst_3_out_4, ledinst_3_out_5,
       ledinst_3_out_6, ledinst_3_out_7, ledinst_4_out_3, ledinst_4_out_4, ledinst_4_out_5, ledinst_4_out_6,
       ledinst_4_out_7, mem_wr_1_do_out, mem_wr_1_ra_out, multiplexer_3_out, multiplexer_4_out,
       multiplexer_6_out, multiplexer_7_out, PC_q, ram_1_data, ram_2_data, unidad_de_registros_1_dato_1,
       unidad_de_registros_1_dato_2;

  Multiplexer #(.width(24)) multiplexer_1 (
    .in0(pc_1), .in1(ex_mem_1_pc_branch_out), .out(multiplexer_1_out), .sel(and_1_out));  // open: en
  Bit_Extender #(.in_width(26), .out_width(24)) bit_extender_1 (.in(ex_mem_1_jump_out), .out(bit_extender_1_out));
  Multiplexer #(.width(24)) multiplexer_2 (
    .in0(multiplexer_1_out), .in1(bit_extender_1_out), .out(multiplexer_2_out), .sel(ex_mem_1_jump_sel_out));  // open: en
  Register #(.width(32)) PC (.D(bit_extender_2_out), .en(hazard_control_1_enable), .Q(PC_q), .clk(clock), .clr(Reset));
  assign bit_extender_2_out = {{8{1'b0}}, multiplexer_2_out};  // Bit_Extender bit_extender_2
  Bit_Extender #(.in_width(32), .out_width(24)) bit_extender_3 (.in(PC_q), .out(bit_extender_3_out));
  Adder #(.width(24)) adder_1 (.a(24'h1), .b(bit_extender_3_out), .out(pc_1));  // open: cin, cout
  Clock clock_1 (.out(clock));
  // Probe on bit_extender_3_out
  RAM #(.addrWidth(24), .dataWidth(32)) ram_1 (
    .addr(bit_extender_3_out), .data(ram_1_data));  // open: sel, clk, ld, clr
  IF_DEC if_dec_1 (
    .clk(clock), .pc_1_in(pc_1), .instruccion_in(ram_1_data), .reset(Reset), .pc_1_out(if_dec_1_pc_1_out),
    .pc_in(bit_extender_3_out), .pc_out(if_dec_1_pc_out), .instruccion_in_2(if_dec_1_instruccion_in_2),
    .enable(hazard_control_1_enable));
  // Probe on if_dec_1_pc_out
  // Probe on decodificador_1_opcode
  UC UC (
    .OpCode(decodificador_1_opcode), .RegDst(UC_regdst), .ALUsrc(addi), .MemToReg(UC_memtoreg),
    .RegWrite(UC_regwrite), .MemRead(UC_memread), .MemWrite(UC_memwrite), .Branch(UC_branch), .ALUOp(UC_aluop));
  Decodificador decodificador_1 (
    .Instruccion(if_dec_1_instruccion_in_2), .Funct(Funct), .RD(decodificador_1_rd), .RT(decodificador_1_rt),
    .RS(decodificador_1_rs), .Opcode(decodificador_1_opcode), .Offset(decodificador_1_offset),
    .Jump(decodificador_1_jump));  // open: Shamt
  LED r (.in(type_inst_1_r));
  type_Inst type_inst_1 (
    .in_1(decodificador_1_opcode), .r(type_inst_1_r), .add(add), .load(load), .store(store), .branch(brach),
    .Jump(Jump));
  LED led_1 (.in(Jump));
  ALUcontrol alucontrol_1 (.ALUOp(UC_aluop), .funct(Funct), .out_3(Selec_de_ALU));
  DotMatrix #(.inputtype("row"), .matrixcols(32), .matrixrows(5)) dotmatrix_1 (
    .row0(ledinst_1_out_3), .row1(ledinst_1_out_4), .row2(ledinst_1_out_5), .row3(ledinst_1_out_6),
    .row4(ledinst_1_out_7));
  LedInst ledinst_1 (
    .ADDI(addi), .out_3(ledinst_1_out_3), .out_4(ledinst_1_out_4), .out_5(ledinst_1_out_5),
    .out_6(ledinst_1_out_6), .out_7(ledinst_1_out_7), .Opcode(decodificador_1_opcode));
  LED led_2 (.in(add));
  LED led_3 (.in(load));
  LED led_4 (.in(store));
  LED led_5 (.in(brach));
  Button button_1 (.out(Reset));
  assign bit_extender_4_out = {{16{1'b0}}, decodificador_1_offset};  // Bit_Extender bit_extender_4
  Unidad_de_Registros unidad_de_registros_1 (
    .reset(Reset), .clk(clock), .rs(decodificador_1_rs), .rt(decodificador_1_rt), .rw(mem_wr_1_rw_out),
    .Result(multiplexer_7_out), .dato_1(unidad_de_registros_1_dato_1), .dato_2(unidad_de_registros_1_dato_2),
    .Regwrite(mem_wr_1_regwrite_out));
  DES_EX des_ex_1 (
    .clk(clock), .pc_1_in(if_dec_1_pc_1_out), .pc_1_out(des_ex_1_pc_1_out),
    .R1_in(unidad_de_registros_1_dato_1), .R1_out(des_ex_1_r1_out), .R2_in(unidad_de_registros_1_dato_2),
    .R2_out(des_ex_1_r2_out), .rd_in(decodificador_1_rd), .rd_out(des_ex_1_rd_out),
    .rt_in(decodificador_1_rt), .rt_out(des_ex_1_rt_out), .pc_in(if_dec_1_pc_out), .pc_out(des_ex_1_pc_out),
    .offset_in(bit_extender_4_out), .offset_out(des_ex_1_offset_out), .RegDst_in(UC_regdst),
    .ALUsrc_in(addi), .MemToReg_in(UC_memtoreg), .RegWrite_in(UC_regwrite), .MemRead_in(UC_memread),
    .MemWrite_in(UC_memwrite), .Branch_in(UC_branch), .ALUOp_in(UC_aluop), .ALUsrc_out(des_ex_1_alusrc_out),
    .MemToReg_out(des_ex_1_memtoreg_out), .RegWrite_out(des_ex_1_regwrite_out),
    .MemRead_out(des_ex_1_memread_out), .MemWrite_out(des_ex_1_memwrite_out),
    .Branch_out(des_ex_1_branch_out), .Selec_de_ALU_in(Selec_de_ALU),
    .Selec_de_ALU_out(des_ex_1_selec_de_alu_out), .jum_Sel_in(Jump), .Jump_in(decodificador_1_jump),
    .Jump_out(des_ex_1_jump_out), .jump_sel_out(des_ex_1_jump_sel_out), .rs_in(decodificador_1_rs),
    .rs_out(des_ex_1_rs_out), .in_22(decodificador_1_opcode), .out_43(des_ex_1_out_43),
    .enable(hazard_control_1_enable), .reset(Reset));  // open: RegDst_out, ALUOp_out
  // Probe on des_ex_1_pc_out
  Multiplexer #(.select(2), .width(32)) multiplexer_3 (
    .in0(des_ex_1_r1_out), .in1(multiplexer_7_out), .in2(ex_mem_1_ra_out), .out(multiplexer_3_out),
    .sel(forwarding_unit_1_forwardb));  // open: in3, en
  Multiplexer #(.select(2), .width(32)) multiplexer_4 (
    .in0(des_ex_1_r2_out), .in1(multiplexer_7_out), .in2(ex_mem_1_ra_out), .out(multiplexer_4_out),
    .sel(forwarding_unit_1_forwarda), .en(undriven));  // open: in3
  Multiplexer #(.width(5)) multiplexer_5 (
    .in0(des_ex_1_rd_out), .in1(des_ex_1_rt_out), .out(multiplexer_5_out), .sel(des_ex_1_alusrc_out));  // open: en
  Pc_brach pc_brach_1 (.pc_1(des_ex_1_pc_1_out), .offset(des_ex_1_offset_out), .pc_brach(pc_brach_1_pc_brach));
  Multiplexer #(.width(32)) multiplexer_6 (
    .in0(multiplexer_4_out), .in1(des_ex_1_offset_out), .out(multiplexer_6_out), .sel(des_ex_1_alusrc_out));  // open: en
  Forwarding_unit forwarding_unit_1 (
    .EX_MEM_RegWrite(ex_mem_1_regwrite_out), .EX_MEM_Rd(ex_mem_1_rd_out), .ID_EX_Rt(des_ex_1_rt_out),
    .ID_EX_Rs(des_ex_1_rs_out), .MEM_WB_RegWr(mem_wr_1_regwrite_out), .MEM_WB_Rd(mem_wr_1_rd_out),
    .ForwardA(forwarding_unit_1_forwarda), .ForwardB(forwarding_unit_1_forwardb),
    .hazard(forwarding_unit_1_hazard));
  DotMatrix #(.inputtype("row"), .matrixcols(32), .matrixrows(5)) dotmatrix_2 (
    .row0(ledinst_2_out_3), .row1(ledinst_2_out_4), .row2(ledinst_2_out_5), .row3(ledinst_2_out_6),
    .row4(ledinst_2_out_7));
  LedInst ledinst_2 (
    .ADDI(des_ex_1_alusrc_out), .out_3(ledinst_2_out_3), .out_4(ledinst_2_out_4), .out_5(ledinst_2_out_5),
    .out_6(ledinst_2_out_6), .out_7(ledinst_2_out_7), .Opcode(des_ex_1_out_43));
  EX_MEM ex_mem_1 (
    .pc_brach_in(pc_brach_1_pc_brach), .pc_branch_out(ex_mem_1_pc_branch_out), .ZERO_in(alu_1_zero),
    .ZERO_out(ex_mem_1_zero_out), .clk(clock), .reset(Reset), .RA_in(alu_1_result), .RA_out(ex_mem_1_ra_out),
    .R2_in(multiplexer_4_out), .R2_out(ex_mem_1_r2_out), .RW_in(multiplexer_5_out), .RW_out(ex_mem_1_rw_out),
    .pc_in(des_ex_1_pc_out), .pc_out(ex_mem_1_pc_out), .MemToReg_in(des_ex_1_memtoreg_out),
    .MemToReg_out(ex_mem_1_memtoreg_out), .RegWrite_in(des_ex_1_regwrite_out),
    .RegWrite_out(ex_mem_1_regwrite_out), .MemRead_in(des_ex_1_memread_out),
    .MemRead_out(ex_mem_1_memread_out), .MemWrite_in(des_ex_1_memwrite_out),
    .MemWrite_out(ex_mem_1_memwrite_out), .Branch_in(des_ex_1_branch_out), .Branch_out(ex_mem_1_branch_out),
    .Jump_in(des_ex_1_jump_out), .Jump_out(ex_mem_1_jump_out), .jum_Sel_in(des_ex_1_jump_sel_out),
    .jump_sel_out(ex_mem_1_jump_sel_out), .rs_in(des_ex_1_rs_out), .rs_out(ex_mem_1_rs_out),
    .rd_in(des_ex_1_rd_out), .rd_out(ex_mem_1_rd_out), .rt_in(des_ex_1_rt_out), .rt_out(ex_mem_1_rt_out),
    .opcode(des_ex_1_out_43), .opcode_2(ex_mem_1_opcode_2), .ALUsrc_in(des_ex_1_alusrc_out),
    .ALUsrc_out(ex_mem_1_alusrc_out), .ena(hazard_control_1_enable));  // open: salida
  ALU alu_1 (
    .DATA1(multiplexer_3_out), .DATA2(multiplexer_6_out), .AluControl(des_ex_1_selec_de_alu_out),
    .RESULT(alu_1_result), .Zero(alu_1_zero));
  // Probe on ex_mem_1_pc_out
  and and_1 (and_1_out, ex_mem_1_branch_out, ex_mem_1_zero_out);
  DotMatrix #(.inputtype("row"), .matrixcols(32), .matrixrows(5)) dotmatrix_3 (
    .row0(ledinst_3_out_3), .row1(ledinst_3_out_4), .row2(ledinst_3_out_5), .row3(ledinst_3_out_6),
    .row4(ledinst_3_out_7));
  LedInst ledinst_3 (
    .ADDI(ex_mem_1_alusrc_out), .out_3(ledinst_3_out_3), .out_4(ledinst_3_out_4), .out_5(ledinst_3_out_5),
    .out_6(ledinst_3_out_6), .out_7(ledinst_3_out_7), .Opcode(ex_mem_1_opcode_2));
  Bit_Extender #(.in_width(32), .out_width(24)) bit_extender_5 (.in(ex_mem_1_ra_out), .out(bit_extender_5_out));
  not not_1 (not_1_out, ex_mem_1_memwrite_out);
  RAM #(.addrWidth(24), .dataWidth(32), .bus("separate")) ram_2 (
    .addr(bit_extender_5_out), .din(ex_mem_1_r2_out), .data(ram_2_data), .clk(clock), .ld(not_1_out),
    .clr(Reset));  // open: str, sel
  Hazard_control hazard_control_1 (
    .ENABLE(hazard_control_1_enable), .EX_MEM_PC(ex_mem_1_pc_out), .MEM_WEB_PC(mem_wr_1_pc_out),
    .ENABLEhAZAR(not_2_out));
  not not_2 (not_2_out, forwarding_unit_1_hazard);
  Mem_Wr mem_wr_1 (
    .RA_in(ex_mem_1_ra_out), .RA_out(mem_wr_1_ra_out), .DO_in(ram_2_data), .DO_out(mem_wr_1_do_out),
    .RW_in(ex_mem_1_rw_out), .RW_out(mem_wr_1_rw_out), .pc_in(ex_mem_1_pc_out), .pc_out(mem_wr_1_pc_out),
    .MemToReg_in(ex_mem_1_memtoreg_out), .MemToReg_out(mem_wr_1_memtoreg_out),
    .RegWrite_in(ex_mem_1_regwrite_out), .RegWrite_out(mem_wr_1_regwrite_out),
    .MemRead_in(ex_mem_1_memread_out), .rs_in(ex_mem_1_rs_out), .rd_in(ex_mem_1_rd_out),
    .rd_out(mem_wr_1_rd_out), .rt_in(ex_mem_1_rt_out), .opcode(ex_mem_1_opcode_2), .out_25(mem_wr_1_out_25),
    .ALUsrc_in(ex_mem_1_alusrc_out), .ALUsrc_out(mem_wr_1_alusrc_out), .clk(clock), .reset(Reset));  // open: MemRead_out, rs_out, rt_out
  // Probe on mem_wr_1_pc_out
  Multiplexer #(.width(32)) multiplexer_7 (
    .in0(mem_wr_1_ra_out), .in1(mem_wr_1_do_out), .out(multiplexer_7_out), .sel(mem_wr_1_memtoreg_out));  // open: en
  LedInst ledinst_4 (
    .ADDI(mem_wr_1_alusrc_out), .out_3(ledinst_4_out_3), .out_4(ledinst_4_out_4), .out_5(ledinst_4_out_5),
    .out_6(ledinst_4_out_6), .out_7(ledinst_4_out_7), .Opcode(mem_wr_1_out_25));
  DotMatrix #(.inputtype("row"), .matrixcols(32), .matrixrows(5)) dotmatrix_4 (
    .row0(ledinst_4_out_3), .row1(ledinst_4_out_4), .row2(ledinst_4_out_5), .row3(ledinst_4_out_6),
    .row4(ledinst_4_out_7));

  // Notes on the sheet:
  //   La instruccion que esta en decode es de tipo:
  //   La instruccion que esta en execute es de tipo:
  //   La instruccion que esta en decode es de tipo:
  //   La instruccion que esta en decode es de tipo:
endmodule

module Decodificador (
  input  [31:0] Instruccion,
  output [5:0] Funct,
  output [4:0] Shamt,
  output [4:0] RD,
  output [4:0] RT,
  output [4:0] RS,
  output [5:0] Opcode,
  output [15:0] Offset,
  output [25:0] Jump
);


  assign Funct = Instruccion[5:0];
  assign Jump = Instruccion[25:0];
  assign Offset = Instruccion[15:0];
  assign Opcode = Instruccion[31:26];
  assign RD = Instruccion[15:11];
  assign RS = Instruccion[25:21];
  assign RT = Instruccion[20:16];
  assign Shamt = Instruccion[10:6];

  // Notes on the sheet:
  //   R
endmodule

module type_Inst (
  input  [5:0] in_1,
  output r,
  output add,
  output load,
  output store,
  output branch,
  output Jump
);

  Comparator #(.width(6)) comparator_1 (.a(in_1), .b({6{1'b0}}), .eq(r));  // open: gt, lt
  Comparator #(.width(6)) comparator_2 (.a(in_1), .b({6{1'b0}}), .eq(add));  // open: gt, lt
  Comparator #(.width(6)) comparator_3 (.a(in_1), .b(6'b100011), .eq(load));  // open: gt, lt
  Comparator #(.width(6)) comparator_4 (.a(in_1), .b(6'b101011), .eq(store));  // open: gt, lt
  Comparator #(.width(6)) comparator_5 (.a(in_1), .b(6'b000100), .eq(branch));  // open: gt, lt
  Comparator #(.width(6)) comparator_6 (.a(in_1), .b(6'b000010), .eq(Jump));  // open: gt, lt
endmodule

// Registros
module Unidad_de_Registros (
  input  reset,
  input  clk,
  input  [4:0] rs,
  input  Regwrite,
  input  [4:0] rt,
  input  [4:0] rw,
  input  [31:0] Result,
  output [31:0] dato_1,
  output [31:0] dato_2
);

  wire a0, a1, a2, a3, a4, a5, a6, a7, a8, a9, a10, a11, a12, a13, a14, a15, a16, a17, a18, a19, a20, a21,
       a22, a23, a24, a25, a26, a27, a28, a29, a30, a31, undriven;
  wire [31:0] R0, R1, R2, R3, R4, R5, R6, R7, R8, R9, R10, R11, R12, R13, R14, R15, R16, R17, R18, R19, R20,
       R21, R22, R23, R24, R25, R26, R27, R28, R29, R30, R31;

  Register #(.width(32)) register_1 (.D(Result), .en(a0), .Q(R0), .clk(clk), .clr(reset));
  Register #(.width(32)) register_2 (.D(Result), .en(a6), .Q(R6), .clk(clk), .clr(reset));
  // Probe on R12
  Register #(.width(32)) register_3 (.D(Result), .en(a12), .Q(R12), .clk(clk), .clr(reset));
  Register #(.width(32)) register_4 (.D(Result), .en(a18), .Q(R18), .clk(clk), .clr(reset));
  Register #(.width(32)) register_5 (.D(Result), .en(a24), .Q(R24), .clk(clk), .clr(reset));
  Register #(.width(32)) register_6 (.D(Result), .en(a30), .Q(R30), .clk(clk), .clr(reset));
  Multiplexer #(.select(5), .width(32)) multiplexer_1 (
    .in0(R0), .in1(R1), .in2(R2), .in3(R3), .in4(R4), .in5(R5), .in6(R6), .in7(R7), .in8(R8), .in9(R9),
    .in10(R10), .in11(R11), .in12(R12), .in13(R13), .in14(R14), .in15(R15), .in16(R16), .in17(R17),
    .in18(R18), .in19(R19), .in20(R20), .in21(R21), .in22(R22), .in23(R23), .in24(R24), .in25(R25),
    .in26(R26), .in27(R27), .in28(R28), .in29(R29), .in30(R30), .in31(R31), .out(dato_1), .sel(rs));  // open: en
  Register #(.width(32)) register_7 (.D(Result), .en(a1), .Q(R1), .clk(clk), .clr(reset));
  Register #(.width(32)) register_8 (.D(Result), .en(a7), .Q(R7), .clk(clk), .clr(reset));
  Register #(.width(32)) register_9 (.D(Result), .en(a13), .Q(R13), .clk(clk), .clr(reset));
  Register #(.width(32)) register_10 (.D(Result), .en(a19), .Q(R19), .clk(clk), .clr(reset));
  Register #(.width(32)) register_11 (.D(Result), .en(a25), .Q(R25), .clk(clk), .clr(reset));
  Register #(.width(32)) register_12 (.D(Result), .en(a31), .Q(R31), .clk(clk), .clr(reset));
  Register #(.width(32)) register_13 (.D(Result), .en(a2), .Q(R2), .clk(clk), .clr(reset));
  Register #(.width(32)) register_14 (.D(Result), .en(a8), .Q(R8), .clk(clk), .clr(reset));
  Register #(.width(32)) register_15 (.D(Result), .en(a14), .Q(R14), .clk(clk), .clr(reset));
  Register #(.width(32)) register_16 (.D(Result), .en(a20), .Q(R20), .clk(clk), .clr(reset));
  Register #(.width(32)) register_17 (.D(Result), .en(a26), .Q(R26), .clk(clk), .clr(reset));
  Multiplexer #(.select(5), .width(32)) multiplexer_2 (
    .in0(R0), .in1(R1), .in2(R2), .in3(R3), .in4(R4), .in5(R5), .in6(R6), .in7(R7), .in8(R8), .in9(R9),
    .in10(R10), .in11(R11), .in12(R12), .in13(R13), .in14(R14), .in15(R15), .in16(R16), .in17(R17),
    .in18(R18), .in19(R19), .in20(R20), .in21(R21), .in22(R22), .in23(R23), .in24(R24), .in25(R25),
    .in26(R26), .in27(R27), .in28(R28), .in29(R29), .in30(R30), .in31(R31), .out(dato_2), .sel(rt),
    .en(undriven));
  Register #(.width(32)) register_18 (.D(Result), .en(a3), .Q(R3), .clk(clk), .clr(reset));
  Register #(.width(32)) register_19 (.D(Result), .en(a9), .Q(R9), .clk(clk), .clr(reset));
  Register #(.width(32)) register_20 (.D(Result), .en(a15), .Q(R15), .clk(clk), .clr(reset));
  Register #(.width(32)) register_21 (.D(Result), .en(a21), .Q(R21), .clk(clk), .clr(reset));
  Register #(.width(32)) register_22 (.D(Result), .en(a27), .Q(R27), .clk(clk), .clr(reset));
  // Probe on R11
  Register #(.width(32)) register_23 (.D(Result), .en(a4), .Q(R4), .clk(clk), .clr(reset));
  Register #(.width(32)) register_24 (.D(Result), .en(a10), .Q(R10), .clk(clk), .clr(reset));
  Register #(.width(32)) register_25 (.D(Result), .en(a16), .Q(R16), .clk(clk), .clr(reset));
  Register #(.width(32)) register_26 (.D(Result), .en(a22), .Q(R22), .clk(clk), .clr(reset));
  Register #(.width(32)) register_27 (.D(Result), .en(a28), .Q(R28), .clk(clk), .clr(reset));
  Demultiplexer #(.select(5)) demultiplexer_1 (
    .out0(a0), .out1(a1), .out2(a2), .out3(a3), .out4(a4), .out5(a5), .out6(a6), .out7(a7), .out8(a8),
    .out9(a9), .out10(a10), .out11(a11), .out12(a12), .out13(a13), .out14(a14), .out15(a15), .out16(a16),
    .out17(a17), .out18(a18), .out19(a19), .out20(a20), .out21(a21), .out22(a22), .out23(a23), .out24(a24),
    .out25(a25), .out26(a26), .out27(a27), .out28(a28), .out29(a29), .out30(a30), .out31(a31), .in(Regwrite),
    .sel(rw));  // open: en
  Register #(.width(32)) register_28 (.D(Result), .en(a5), .Q(R5), .clk(clk), .clr(reset));
  Register #(.width(32)) register_29 (.D(Result), .en(a11), .Q(R11), .clk(clk), .clr(reset));
  Register #(.width(32)) register_30 (.D(Result), .en(a17), .Q(R17), .clk(clk), .clr(reset));
  Register #(.width(32)) register_31 (.D(Result), .en(a23), .Q(R23), .clk(clk), .clr(reset));
  Register #(.width(32)) register_32 (.D(Result), .en(a29), .Q(R29), .clk(clk), .clr(reset));

  // Other names for the same wires on the sheet: clock = clk; Direccion1[4:0] = rs; Direccion2[4:0] = rt;
  //   Direccion3[4:0] = rw; Direccion4[31:0] = Result
endmodule

module UCA (
  input  [1:0] ALUOp,
  input  [5:0] Func,
  output [3:0] out_3
);

  wire and_1_out, and_2_out, and_3_out, and_4_out, not_1_out, not_2_out, not_3_out;

  not not_1 (not_1_out, ALUOp[0]);
  not not_2 (not_2_out, ALUOp[0]);
  not not_3 (not_3_out, Func[2]);
  and and_1 (and_1_out, ALUOp[0], Func[0]);
  and and_2 (and_2_out, ALUOp[0], Func[3]);
  and and_3 (and_3_out, not_1_out, ALUOp[1]);
  and and_4 (and_4_out, ALUOp[0], Func[1]);
  or or_1 (out_3[1], not_2_out, not_3_out);
  or or_2 (out_3[0], and_1_out, and_2_out);
  or or_3 (out_3[2], and_3_out, and_4_out);

  assign out_3[3] = 1'b0;
endmodule

// UC
module UC (
  input  [5:0] OpCode,
  output RegDst,
  output ALUsrc,
  output MemToReg,
  output RegWrite,
  output MemRead,
  output MemWrite,
  output Branch,
  output [1:0] ALUOp
);

  wire and_2_out, and_3_out, not_2_out, not_3_out, not_4_out, not_5_out, not_6_out, not_7_out, not_8_out,
       not_9_out, not_10_out, not_11_out, not_12_out, not_13_out, not_14_out, not_15_out, not_16_out,
       not_17_out;

  not not_1 (RegDst, OpCode[5]);
  or or_1 (ALUsrc, OpCode[3], OpCode[1]);
  not not_2 (not_2_out, OpCode[2]);
  not not_3 (not_3_out, OpCode[3]);
  not not_4 (not_4_out, OpCode[2]);
  not not_5 (not_5_out, OpCode[5]);
  not not_6 (not_6_out, OpCode[3]);
  and and_1 (MemWrite, OpCode[0], OpCode[3]);
  not not_7 (not_7_out, OpCode[5]);
  not not_8 (not_8_out, OpCode[4]);
  not not_9 (not_9_out, OpCode[3]);
  not not_10 (not_10_out, OpCode[2]);
  not not_11 (not_11_out, OpCode[1]);
  not not_12 (not_12_out, OpCode[0]);
  not not_13 (not_13_out, OpCode[5]);
  not not_14 (not_14_out, OpCode[4]);
  not not_15 (not_15_out, OpCode[3]);
  not not_16 (not_16_out, OpCode[1]);
  not not_17 (not_17_out, OpCode[0]);
  and and_2 (and_2_out, not_2_out, not_3_out);
  and and_3 (and_3_out, not_4_out, not_5_out);
  and and_4 (MemRead, OpCode[1], not_6_out);
  or or_2 (RegWrite, and_2_out, and_3_out);
  and and_5 (ALUOp[1], not_7_out, not_8_out, not_9_out, not_10_out, not_11_out, not_12_out);
  and and_6 (ALUOp[0], not_13_out, not_14_out, not_15_out, OpCode[2], not_16_out, not_17_out);

  assign Branch = OpCode[2];
  assign MemToReg = OpCode[1];
endmodule

module IF_DEC (
  input  clk,
  input  reset,
  input  [23:0] pc_1_in,
  input  [31:0] instruccion_in,
  input  [23:0] pc_in,
  input  enable,
  output [23:0] pc_1_out,
  output [31:0] instruccion_in_2,
  output [23:0] pc_out
);

  Register #(.width(24)) register_1 (.D(pc_1_in), .en(enable), .Q(pc_1_out), .clk(clk), .clr(reset));
  Register #(.width(32)) register_2 (.D(instruccion_in), .en(enable), .Q(instruccion_in_2), .clk(clk), .clr(reset));
  Register #(.width(24)) register_3 (.D(pc_in), .en(enable), .Q(pc_out), .clk(clk), .clr(reset));

  // Other names for the same wires on the sheet: ena = enable; res = reset
endmodule

module DES_EX (
  input  clk,
  input  reset,
  input  [23:0] pc_1_in,
  input  [31:0] R1_in,
  input  [31:0] R2_in,
  input  [31:0] offset_in,
  input  [4:0] rs_in,
  input  [4:0] rd_in,
  input  [4:0] rt_in,
  input  [23:0] pc_in,
  input  [25:0] Jump_in,
  input  jum_Sel_in,
  input  RegDst_in,
  input  ALUsrc_in,
  input  MemToReg_in,
  input  RegWrite_in,
  input  MemRead_in,
  input  MemWrite_in,
  input  Branch_in,
  input  [1:0] ALUOp_in,
  input  [3:0] Selec_de_ALU_in,
  input  [5:0] in_22,
  input  enable,
  output [23:0] pc_1_out,
  output [31:0] R1_out,
  output [31:0] R2_out,
  output [31:0] offset_out,
  output [4:0] rs_out,
  output [4:0] rd_out,
  output [4:0] rt_out,
  output [23:0] pc_out,
  output [25:0] Jump_out,
  output jump_sel_out,
  output RegDst_out,
  output ALUsrc_out,
  output MemToReg_out,
  output RegWrite_out,
  output MemRead_out,
  output MemWrite_out,
  output Branch_out,
  output [1:0] ALUOp_out,
  output [3:0] Selec_de_ALU_out,
  output [5:0] out_43
);

  Register #(.width(1)) register_1 (.D(jum_Sel_in), .en(enable), .Q(jump_sel_out), .clk(clk), .clr(reset));
  Register #(.width(24)) register_2 (.D(pc_1_in), .en(enable), .Q(pc_1_out), .clk(clk), .clr(reset));
  Register #(.width(32)) register_3 (.D(R1_in), .en(enable), .Q(R1_out), .clk(clk), .clr(reset));
  Register #(.width(32)) register_4 (.D(R2_in), .en(enable), .Q(R2_out), .clk(clk), .clr(reset));
  Register #(.width(32)) register_5 (.D(offset_in), .en(enable), .Q(offset_out), .clk(clk), .clr(reset));
  Register #(.width(5)) register_6 (.D(rs_in), .en(enable), .Q(rs_out), .clk(clk), .clr(reset));
  Register #(.width(5)) register_7 (.D(rd_in), .en(enable), .Q(rd_out), .clk(clk), .clr(reset));
  Register #(.width(5)) register_8 (.D(rt_in), .en(enable), .Q(rt_out), .clk(clk), .clr(reset));
  Register #(.width(24)) register_9 (.D(pc_in), .en(enable), .Q(pc_out), .clk(clk), .clr(reset));
  Register #(.width(26)) register_10 (.D(Jump_in), .en(enable), .Q(Jump_out), .clk(clk), .clr(reset));
  Register #(.width(1)) register_11 (.D(RegDst_in), .en(enable), .Q(RegDst_out), .clk(clk), .clr(reset));
  Register #(.width(1)) register_12 (.D(ALUsrc_in), .en(enable), .Q(ALUsrc_out), .clk(clk), .clr(reset));
  Register #(.width(1)) register_13 (.D(MemToReg_in), .en(enable), .Q(MemToReg_out), .clk(clk), .clr(reset));
  Register #(.width(1)) register_14 (.D(RegWrite_in), .en(enable), .Q(RegWrite_out), .clk(clk), .clr(reset));
  Register #(.width(1)) register_15 (.D(MemRead_in), .en(enable), .Q(MemRead_out), .clk(clk), .clr(reset));
  Register #(.width(1)) register_16 (.D(MemWrite_in), .en(enable), .Q(MemWrite_out), .clk(clk), .clr(reset));
  Register #(.width(1)) register_17 (.D(Branch_in), .en(enable), .Q(Branch_out), .clk(clk), .clr(reset));
  Register #(.width(2)) register_18 (.D(ALUOp_in), .en(enable), .Q(ALUOp_out), .clk(clk), .clr(reset));
  Register #(.width(4)) register_19 (.D(Selec_de_ALU_in), .en(enable), .Q(Selec_de_ALU_out), .clk(clk), .clr(reset));
  Register #(.width(6)) register_20 (.D(in_22), .en(enable), .Q(out_43), .clk(clk), .clr(reset));

  // Other names for the same wires on the sheet: res = reset
endmodule

module EX_MEM (
  input  clk,
  input  reset,
  input  ena,
  input  [23:0] pc_brach_in,
  input  ZERO_in,
  input  [31:0] RA_in,
  input  [31:0] R2_in,
  input  [4:0] RW_in,
  input  [4:0] rs_in,
  input  [4:0] rd_in,
  input  [4:0] rt_in,
  input  [23:0] pc_in,
  input  [25:0] Jump_in,
  input  jum_Sel_in,
  input  ALUsrc_in,
  input  MemToReg_in,
  input  RegWrite_in,
  input  MemRead_in,
  input  MemWrite_in,
  input  Branch_in,
  input  [5:0] opcode,
  output [23:0] pc_branch_out,
  output [1:0] salida,
  output ZERO_out,
  output [31:0] RA_out,
  output [31:0] R2_out,
  output [4:0] RW_out,
  output [4:0] rs_out,
  output [4:0] rd_out,
  output [4:0] rt_out,
  output [23:0] pc_out,
  output [25:0] Jump_out,
  output jump_sel_out,
  output ALUsrc_out,
  output MemToReg_out,
  output RegWrite_out,
  output MemRead_out,
  output MemWrite_out,
  output Branch_out,
  output [5:0] opcode_2
);

  wire comparator_1_eq, res;

  Register #(.width(24)) register_1 (.D(pc_brach_in), .en(ena), .Q(pc_branch_out), .clk(clk), .clr(res));
  Register #(.width(1)) register_2 (.D(ZERO_in), .en(ena), .Q(ZERO_out), .clk(clk), .clr(res));
  Register #(.width(32)) register_3 (.D(RA_in), .en(ena), .Q(RA_out), .clk(clk), .clr(res));
  Register #(.width(32)) register_4 (.D(R2_in), .en(ena), .Q(R2_out), .clk(clk), .clr(res));
  Register #(.width(5)) register_5 (.D(RW_in), .en(ena), .Q(RW_out), .clk(clk), .clr(res));
  Register #(.width(5)) register_6 (.D(rs_in), .en(ena), .Q(rs_out), .clk(clk), .clr(res));
  Register #(.width(5)) register_7 (.D(rd_in), .en(ena), .Q(rd_out), .clk(clk), .clr(res));
  Register #(.width(5)) register_8 (.D(rt_in), .en(ena), .Q(rt_out), .clk(clk), .clr(res));
  Register #(.width(24)) register_9 (.D(pc_in), .en(ena), .Q(pc_out), .clk(clk), .clr(res));
  Register #(.width(26)) register_10 (.D(Jump_in), .en(ena), .Q(Jump_out), .clk(clk), .clr(res));
  Register #(.width(1)) register_11 (.D(jum_Sel_in), .en(ena), .Q(jump_sel_out), .clk(clk), .clr(res));
  Register #(.width(1)) register_12 (.D(ALUsrc_in), .en(ena), .Q(ALUsrc_out), .clk(clk), .clr(res));
  Register #(.width(1)) register_13 (.D(MemToReg_in), .en(ena), .Q(MemToReg_out), .clk(clk), .clr(res));
  Register #(.width(1)) register_14 (.D(RegWrite_in), .en(ena), .Q(RegWrite_out), .clk(clk), .clr(res));
  Register #(.width(1)) register_15 (.D(MemRead_in), .en(ena), .Q(MemRead_out), .clk(clk), .clr(res));
  Register #(.width(1)) register_16 (.D(MemWrite_in), .en(ena), .Q(MemWrite_out), .clk(clk), .clr(res));
  Register #(.width(1)) register_17 (.D(Branch_in), .en(ena), .Q(Branch_out), .clk(clk), .clr(res));
  Register #(.width(6)) register_18 (.D(opcode), .en(ena), .Q(opcode_2), .clk(clk), .clr(res));
  Multiplexer multiplexer_1 (.in0(comparator_1_eq), .in1(reset), .out(res), .sel(ena));  // open: en
  Counter #(.width(2), .max('h1)) counter_1 (.D(2'b01), .Q(salida), .clk(clk), .clr(ena));  // open: load, count, carry
  Comparator #(.width(2)) comparator_1 (.a(2'b01), .b(salida), .eq(comparator_1_eq));  // open: gt, lt

  // Other names for the same wires on the sheet: rex = reset
endmodule

module Mem_Wr (
  input  clk,
  input  reset,
  input  [31:0] RA_in,
  input  [31:0] DO_in,
  input  [4:0] RW_in,
  input  [23:0] pc_in,
  input  [4:0] rs_in,
  input  [4:0] rd_in,
  input  [4:0] rt_in,
  input  MemToReg_in,
  input  RegWrite_in,
  input  MemRead_in,
  input  [5:0] opcode,
  input  ALUsrc_in,
  output [31:0] RA_out,
  output [31:0] DO_out,
  output [4:0] RW_out,
  output [23:0] pc_out,
  output [4:0] rs_out,
  output [4:0] rd_out,
  output [4:0] rt_out,
  output MemToReg_out,
  output RegWrite_out,
  output MemRead_out,
  output [5:0] out_25,
  output ALUsrc_out
);

  Register #(.width(32)) register_1 (.D(RA_in), .Q(RA_out), .clk(clk), .clr(reset));  // open: en
  Register #(.width(32)) register_2 (.D(DO_in), .Q(DO_out), .clk(clk), .clr(reset));  // open: en
  Register #(.width(5)) register_3 (.D(RW_in), .Q(RW_out), .clk(clk), .clr(reset));  // open: en
  Register #(.width(24)) register_4 (.D(pc_in), .Q(pc_out), .clk(clk), .clr(reset));  // open: en
  Register #(.width(5)) register_5 (.D(rs_in), .Q(rs_out), .clk(clk), .clr(reset));  // open: en
  Register #(.width(5)) register_6 (.D(rd_in), .Q(rd_out), .clk(clk), .clr(reset));  // open: en
  Register #(.width(5)) register_7 (.D(rt_in), .Q(rt_out), .clk(clk), .clr(reset));  // open: en
  Register #(.width(1)) register_8 (.D(MemToReg_in), .Q(MemToReg_out), .clk(clk), .clr(reset));  // open: en
  Register #(.width(1)) register_9 (.D(RegWrite_in), .Q(RegWrite_out), .clk(clk), .clr(reset));  // open: en
  Register #(.width(1)) register_10 (.D(MemRead_in), .Q(MemRead_out), .clk(clk), .clr(reset));  // open: en
  Register #(.width(6)) register_11 (.D(opcode), .Q(out_25), .clk(clk), .clr(reset));  // open: en
  Register #(.width(1)) register_12 (.D(ALUsrc_in), .Q(ALUsrc_out), .clk(clk), .clr(reset));  // open: en

  // Other names for the same wires on the sheet: res = reset
endmodule

// pc_brach
module Pc_brach (
  input  [23:0] pc_1,
  input  [31:0] offset,
  output [23:0] pc_brach
);

  wire [15:0] bit_extender_1_out;
  wire [23:0] adder_1_out, bit_extender_2_out, subtractor_1_out;

  Bit_Extender #(.in_width(32)) bit_extender_1 (.in(offset), .out(bit_extender_1_out));
  assign bit_extender_2_out = {{9{1'b0}}, bit_extender_1_out[14:0]};  // Bit_Extender bit_extender_2
  Adder #(.width(24)) adder_1 (.a(pc_1), .b(bit_extender_2_out), .out(adder_1_out));  // open: cin, cout
  Subtractor #(.width(24)) subtractor_1 (.a(pc_1), .b(bit_extender_2_out), .out(subtractor_1_out));  // open: bin, bout
  Multiplexer #(.width(24)) multiplexer_1 (
    .in0(adder_1_out), .in1(subtractor_1_out), .out(pc_brach), .sel(bit_extender_1_out[15]));  // open: en
endmodule

module LedInst (
  input  [5:0] Opcode,
  input  ADDI,
  output [31:0] out_3,
  output [31:0] out_4,
  output [31:0] out_5,
  output [31:0] out_6,
  output [31:0] out_7
);

  wire [2:0] Slct;
  wire [5:1] type_inst_1_add;

  type_Inst type_inst_1 (
    .in_1(Opcode), .add(type_inst_1_add[1]), .load(type_inst_1_add[2]), .store(type_inst_1_add[3]),
    .branch(type_inst_1_add[4]), .Jump(type_inst_1_add[5]));  // open: r
  // Probe on Slct
  BitFinder #(.width(7), .\type ("high1")) bitfinder_1 (
    .in({ADDI, type_inst_1_add, 1'b0}), .index(Slct));  // open: found
  Multiplexer #(.select(3), .width(32), .enable("false")) multiplexer_1 (
    .in1(32'h67380000), .in2(32'h8f19c000), .in3(32'h6f98c780), .in4(32'h7798ce90), .in5(32'hfa58b800),
    .in6(32'h67390000), .out(out_3), .sel(Slct));  // open: in0, in7
  Multiplexer #(.select(3), .width(32), .enable("false")) multiplexer_2 (
    .in1(32'h94a40000), .in2(32'h89252000), .in3(32'h82252400), .in4(32'h94a52890), .in5(32'h2255a400),
    .in6(32'h94a50000), .out(out_4), .sel(Slct));  // open: in0, in7
  Multiplexer #(.select(3), .width(32), .enable("false")) multiplexer_3 (
    .in1(32'h94a40000), .in2(32'h89252000), .in3(32'h62254780), .in4(32'hf72528f0), .in5(32'h2252b800),
    .in6(32'h94a50000), .out(out_5), .sel(Slct));  // open: in0, in7
  Multiplexer #(.select(3), .width(32), .enable("false")) multiplexer_4 (
    .in1(32'hf4a40000), .in2(32'h893d2000), .in3(32'h12252400), .in4(32'h953d2890), .in5(32'h2250a000),
    .in6(32'hf4a50000), .out(out_6), .sel(Slct));  // open: in0, in7
  Multiplexer #(.select(3), .width(32), .enable("false")) multiplexer_5 (
    .in1(32'h97bc0000), .in2(32'hef25e000), .in3(32'he2191780), .in4(32'hf4a52e90), .in5(32'he190a000),
    .in6(32'h97bd0000), .out(out_7), .sel(Slct));  // open: in0, in7
endmodule

// Data_Hazard_detec
module Forwarding_unit (
  input  EX_MEM_RegWrite,
  input  [4:0] EX_MEM_Rd,
  input  [4:0] ID_EX_Rt,
  input  [4:0] ID_EX_Rs,
  input  MEM_WB_RegWr,
  input  [4:0] MEM_WB_Rd,
  output hazard,
  output [1:0] ForwardA,
  output [1:0] ForwardB
);

  wire comparator_1_eq, comparator_2_eq, comparator_3_eq, comparator_4_eq, comparator_5_eq, comparator_6_eq,
       comparator_7_eq, comparator_8_eq;

  Comparator #(.width(5)) comparator_1 (.a(EX_MEM_Rd), .b({5{1'b0}}), .eq(comparator_1_eq));  // open: gt, lt
  Comparator #(.width(5)) comparator_2 (.a(EX_MEM_Rd), .b(ID_EX_Rs), .eq(comparator_2_eq));  // open: gt, lt
  Comparator #(.width(5)) comparator_3 (.a(EX_MEM_Rd), .b(ID_EX_Rt), .eq(comparator_3_eq));  // open: gt, lt
  Comparator #(.width(5)) comparator_4 (.a({5{1'b0}}), .b(MEM_WB_Rd), .eq(comparator_4_eq));  // open: gt, lt
  Comparator #(.width(5)) comparator_5 (.a(EX_MEM_Rd), .b(ID_EX_Rs), .eq(comparator_5_eq));  // open: gt, lt
  Comparator #(.width(5)) comparator_6 (.a(MEM_WB_Rd), .b(ID_EX_Rs), .eq(comparator_6_eq));  // open: gt, lt
  Comparator #(.width(5)) comparator_7 (.a(EX_MEM_Rd), .b(ID_EX_Rt), .eq(comparator_7_eq));  // open: gt, lt
  Comparator #(.width(5)) comparator_8 (.a(MEM_WB_Rd), .b(ID_EX_Rt), .eq(comparator_8_eq));  // open: gt, lt
  and and_1 (ForwardA[1], ~comparator_1_eq, EX_MEM_RegWrite, comparator_2_eq);  // AND_Gate
  and and_2 (ForwardB[1], ~comparator_1_eq, comparator_3_eq, EX_MEM_RegWrite);  // AND_Gate
  and and_3 (ForwardA[0], MEM_WB_RegWr, ~comparator_4_eq, ~comparator_5_eq, comparator_6_eq);  // AND_Gate
  and and_4 (ForwardB[0], MEM_WB_RegWr, ~comparator_4_eq, ~comparator_7_eq, comparator_8_eq);  // AND_Gate
  or or_1 (hazard, ForwardA[1], ForwardB[1], ForwardA[0], ForwardB[0]);

  // Notes on the sheet:
  //   1if-> fa=2  10
  //   2if ->fb= 2 10
  //   3if ->fa =1 01
  //   4 if ->fb= 1 01
endmodule

module ALUcontrol (
  input  [1:0] ALUOp,
  input  [5:0] funct,
  output [3:0] out_3
);

  wire and_1_out, and_2_out, and_3_out, and_4_out, and_5_out, and_6_out, not_1_out, not_2_out, not_3_out,
       not_4_out, not_5_out, not_6_out, not_7_out, not_8_out;

  not not_1 (not_1_out, ALUOp[1]);
  not not_2 (not_2_out, funct[2]);
  not not_3 (not_3_out, ALUOp[1]);
  not not_4 (not_4_out, funct[2]);
  not not_5 (not_5_out, funct[3]);
  not not_6 (not_6_out, funct[1]);
  not not_7 (not_7_out, funct[2]);
  not not_8 (not_8_out, funct[0]);
  and and_1 (and_1_out, not_1_out, ALUOp[0]);
  and and_2 (and_2_out, ALUOp[1], not_2_out, funct[0]);
  and and_3 (and_3_out, ALUOp[1], funct[1]);
  and and_4 (and_4_out, ALUOp[1], funct[3]);
  or or_1 (out_3[1], not_3_out, not_4_out, funct[1], funct[3]);
  and and_5 (and_5_out, ALUOp[1], not_5_out, funct[2], not_6_out, funct[0]);
  and and_6 (and_6_out, ALUOp[1], funct[3], not_7_out, funct[1], not_8_out);
  or or_2 (out_3[2], and_1_out, and_2_out, and_3_out, and_4_out);
  or or_3 (out_3[0], and_5_out, and_6_out);

  assign out_3[3] = 1'b0;
endmodule

module ALU (
  input  [31:0] DATA1,
  input  [31:0] DATA2,
  input  [3:0] AluControl,
  output [31:0] RESULT,
  output Zero
);

  wire comparator_1_eq, comparator_2_eq, comparator_3_eq, comparator_4_eq;
  wire [2:0] priority_encoder_1_out;
  wire [31:0] add, \and , \or , Sub;

  Comparator #(.width(4)) comparator_1 (.a(AluControl), .b(4'b0010), .eq(comparator_1_eq));  // open: gt, lt
  Comparator #(.width(4)) comparator_2 (.a(AluControl), .b(4'b0110), .eq(comparator_2_eq));  // open: gt, lt
  Comparator #(.width(4)) comparator_3 (.a(AluControl), .b(4'b0000), .eq(comparator_3_eq));  // open: gt, lt
  Comparator #(.width(4)) comparator_4 (.a(AluControl), .b(4'b0001), .eq(comparator_4_eq));  // open: gt, lt
  Adder #(.width(32)) adder_1 (.a(DATA1), .b(DATA2), .out(add));  // open: cin, cout
  Subtractor #(.width(32)) subtractor_1 (.a(DATA1), .b(DATA2), .out(Sub));  // open: bin, bout
  Comparator #(.width(32)) comparator_5 (.a(DATA1), .b(DATA2), .eq(Zero));  // open: gt, lt
  Priority_Encoder priority_encoder_1 (
    .in0(comparator_1_eq), .in1(comparator_2_eq), .in2(comparator_3_eq), .in3(comparator_4_eq),
    .out(priority_encoder_1_out));  // open: in4, in5, in6, in7, en_in, gs, en_out
  assign \and  = DATA1 & DATA2;  // AND_Gate and_1, 32 bits wide
  assign \or  = DATA1 | DATA2;  // OR_Gate or_1, 32 bits wide
  Multiplexer #(.select(3), .width(32), .enable("false")) multiplexer_1 (
    .in0(add), .in1(Sub), .in2(\and ), .in3(\or ), .out(RESULT), .sel(priority_encoder_1_out));  // open: in4, in5, in6, in7

  // Other names for the same wires on the sheet: A[31:0] = DATA1; B[31:0] = DATA2

  // Notes on the sheet:
  //   Add
  //   0010
  //   Substract
  //   0110
  //   and
  //   0000
  //   or
  //   0001
endmodule

module UnidadControl (
  input  ADDI,
  input  [5:0] OP,
  output RegDst,
  output AluSrc,
  output MentoReg,
  output RegWrite,
  output MenRead,
  output MenWrite,
  output Branch,
  output TipoR,
  output [1:0] ALUOp
);

  wire and_1_out, and_2_out, and_3_out, and_4_out, not_1_out, not_2_out, not_3_out, not_4_out, not_5_out,
       not_6_out, not_7_out, not_8_out, not_9_out, not_10_out, not_11_out, not_12_out, not_13_out,
       not_14_out, not_15_out, not_16_out, not_17_out, not_18_out, not_19_out, not_20_out, not_21_out,
       not_22_out, not_23_out, not_24_out, not_25_out, not_26_out, not_27_out;

  Comparator #(.width(6)) comparator_1 (.a(OP), .b({6{1'b0}}), .eq(TipoR));  // open: gt, lt
  not not_1 (not_1_out, OP[1]);
  not not_2 (not_2_out, OP[2]);
  not not_3 (not_3_out, OP[4]);
  not not_4 (not_4_out, OP[5]);
  not not_5 (not_5_out, OP[5]);
  not not_6 (not_6_out, OP[4]);
  not not_7 (not_7_out, OP[2]);
  not not_8 (not_8_out, OP[1]);
  not not_9 (not_9_out, OP[0]);
  not not_10 (not_10_out, OP[3]);
  not not_11 (not_11_out, OP[1]);
  not not_12 (not_12_out, ADDI);
  and and_1 (and_1_out, not_1_out, not_2_out, OP[3], not_3_out, not_4_out);
  and and_2 (and_2_out, not_5_out, not_6_out, not_7_out, not_8_out, not_9_out);
  not not_13 (not_13_out, OP[3]);
  and and_3 (and_3_out, not_13_out, not_14_out);
  not not_14 (not_14_out, OP[2]);
  and and_4 (and_4_out, not_10_out, OP[1]);
  and and_5 (RegDst, not_11_out, not_12_out);
  or or_1 (AluSrc, OP[1], and_1_out);
  or or_2 (RegWrite, and_2_out, and_3_out);
  not not_15 (not_15_out, ADDI);
  and and_6 (MenWrite, OP[3], not_16_out);
  not not_16 (not_16_out, ADDI);
  not not_17 (not_17_out, OP[5]);
  not not_18 (not_18_out, OP[4]);
  not not_19 (not_19_out, OP[3]);
  not not_20 (not_20_out, OP[2]);
  not not_21 (not_21_out, OP[1]);
  not not_22 (not_22_out, OP[0]);
  not not_23 (not_23_out, OP[5]);
  not not_24 (not_24_out, OP[4]);
  not not_25 (not_25_out, OP[3]);
  not not_26 (not_26_out, OP[1]);
  not not_27 (not_27_out, OP[0]);
  and and_7 (MenRead, and_4_out, not_15_out);
  and and_8 (ALUOp[1], not_17_out, not_18_out, not_19_out, not_20_out, not_21_out, not_22_out);
  and and_9 (ALUOp[0], not_23_out, not_24_out, not_25_out, OP[2], not_26_out, not_27_out);

  assign Branch = OP[2];
  assign MentoReg = OP[1];
endmodule

// Hazard_Control
module Hazard_control (
  input  [23:0] EX_MEM_PC,
  input  [23:0] MEM_WEB_PC,
  input  ENABLEhAZAR,
  output ENABLE
);

  wire and_1_out, comparator_1_eq, comparator_2_eq, not_1_out;

  Comparator #(.width(24)) comparator_1 (.a(EX_MEM_PC), .b({24{1'b0}}), .eq(comparator_1_eq));  // open: gt, lt
  Comparator #(.width(24)) comparator_2 (.a(MEM_WEB_PC), .b(EX_MEM_PC), .eq(comparator_2_eq));  // open: gt, lt
  not not_1 (not_1_out, comparator_2_eq);
  and and_1 (and_1_out, not_1_out, comparator_1_eq);
  or or_1 (ENABLE, and_1_out, ENABLEhAZAR);
endmodule
